// Logisim project Speed_RGB_LED.circ as structural Verilog: 2 circuits, main circuit main
module main (
  input  Computer_D0
);

  wire Computer_CS_out, d_ff_1_q, d_ff_1_qn, d_ff_2_q, or_1_out, RESET_out, Toggle_out, undriven, undriven_2;

  Button Toggle (.out(Toggle_out));
  Button Computer_CS (.out(Computer_CS_out));
  Button RESET (.out(RESET_out));
  D_Flip_Flop d_ff_1 (.D(d_ff_1_qn), .clk(Toggle_out), .Q(d_ff_1_q), .Qn(d_ff_1_qn), .preset(1'b0), .reset(RESET_out));
  D_Flip_Flop d_ff_2 (
    .D(Computer_D0), .clk(Computer_CS_out), .Q(d_ff_2_q), .preset(1'b0), .reset(RESET_out));  // open: Qn
  or or_1 (or_1_out, Toggle_out, Computer_CS_out);
  D_Flip_Flop d_ff_3 ();  // open: D, clk, Q, Qn, preset, reset
  LED led_1 (.in(undriven));
  LED led_2 (.in(undriven_2));
endmodule

module TURBO2 (
  input  CLK,
  input  CPU,
  input  TOG,
  output D
);

  wire nand_1_out, nand_2_out, nand_3_out;

  nand nand_1 (nand_1_out, 1'b1, CLK);
  nand nand_2 (nand_2_out, nand_1_out, TOG);
  nand nand_3 (nand_3_out, CLK, CPU);
  nand nand_4 (D, nand_2_out, nand_3_out);
endmodule
